# Fritzing sketch rainSensor (saved by Fritzing 0.9.3b)
circuit board: 7.11024cm x 6.16614cm
breadboards: 1

parts:
  HLK-PM1 = HLK-PM01
  YL-83_-_Detection_Board1 = YL-83 Rain Sensor - Detection Board
  J1 = female pin header, 1 pin [form="♀ (female)"]
  J2 = female pin header, 1 pin [form="♀ (female)"]
  MCP1 = MCP3008 [part_number=gjhN package="DIP (Dual Inline) [THT]"]
  Mod1 = YL-83 Rain Sensor - Control Board
  Raspberry_Pi_Zero1 = Raspberry Pi Zero

nets:
  N1: HLK-PM1.AC#0, J2.pin1
  N2: HLK-PM1.AC#1, J1.pin1
  GND: HLK-PM1.-Vo, MCP1.2Y3, MCP1.2A, Mod1.GND, Raspberry_Pi_Zero1.GND
  N3: HLK-PM1.+Vo, Raspberry_Pi_Zero1.5V
  N4: YL-83_-_Detection_Board1.POS, Mod1.POS
  N5: YL-83_-_Detection_Board1.NEG, Mod1.NEG
  N6: MCP1.1G_, Mod1.AO
  N7: MCP1.2Y2, Raspberry_Pi_Zero1.GIPO8
  N8: MCP1.2Y1, Raspberry_Pi_Zero1.GIPO10
  N9: MCP1.2Y0, Raspberry_Pi_Zero1.GIPO9
  N10: MCP1.2B, Raspberry_Pi_Zero1.GIPO11
  VCC: MCP1.2G_, MCP1.VCC, Mod1.VCC, Raspberry_Pi_Zero1.3v3, Raspberry_Pi_Zero1.3V3

custom parts:
  YL-83 Rain Sensor - Detection Board: The YL-83 is a rain sensor that has more resistance when dry and less resistance when wet. The module runs at 5V.
  MCP3008: A Dual 2 to 4 DEMX / Decoder
  YL-83 Rain Sensor - Control Board: The YL-83 is a rain sensor that has more resistance when dry and less resistance when wet. The module runs at 5V.
