# Fritzing sketch rainSensor_new (saved by Fritzing 0.9.10b)
circuit board: 6.5cm x 5.64444cm
breadboards: 1

parts:
  Raspberry = Raspberry Pi 4B
  MCP1 = MCP3008 [part_number=gjhN package="DIP (Dual Inline) [THT]"]
  HLK-PM1 = HLK-PM12 [part_number=HLK-PM12]
  J1 = female pin header, 1 pin [form="♀ (female)"]
  J2 = female pin header, 1 pin [form="♀ (female)"]
  YL-83 = YL-83 Rain Sensor - Control Board

nets:
  VCC: Raspberry.5V, MCP1.2G_, MCP1.VCC, HLK-PM1.+Vo, YL-83.VCC
  GND: Raspberry.GND, Raspberry.GPIO7, MCP1.2Y3, MCP1.2A, HLK-PM1.-Vo, YL-83.GND
  N1: Raspberry.GPIO10, MCP1.2Y0
  N2: Raspberry.GPIO9, MCP1.2B
  N3: Raspberry.GPIO25, MCP1.2Y2
  N4: MCP1.1G_, YL-83.AO
  N5: HLK-PM1.AC_1, J2.pin1
  N6: HLK-PM1.AC_2, J1.pin1

custom parts:
  MCP3008: A Dual 2 to 4 DEMX / Decoder
  YL-83 Rain Sensor - Control Board: The YL-83 is a rain sensor that has more resistance when dry and less resistance when wet. The module runs at 5V.
